// Logisim project 7seg.circ as structural Verilog: 1 circuit, main circuit main
module main (
  input  A,
  input  B,
  input  C,
  input  D,
  input  in_5,
  input  in_6,
  output A_seg,
  output B_seg,
  output C_seg,
  output D_seg,
  output E_seg,
  output F_seg,
  output G_seg,
  output out_14
);

  wire and_1_out, and_2_out, and_3_out, and_4_out, and_5_out, and_6_out, and_7_out, and_8_out, and_9_out,
       and_10_out, and_11_out, notA_out, notB_out, notC_out, notD_out, or_1_out, or_2_out, or_4_out,
       or_6_out, or_7_out, or_8_out, or_11_out, xnor_1_out, xnor_2_out, xor_1_out;

  not notA (notA_out, A);
  not notB (notB_out, B);
  not notC (notC_out, C);
  not notD (notD_out, D);
  xnor xnor_1 (xnor_1_out, C, D);
  or or_1 (or_1_out, B, notC_out);
  and and_1 (and_1_out, notB_out, C);
  and and_2 (and_2_out, notB_out, notD_out);
  and and_3 (and_3_out, B, notC_out);
  and and_4 (and_4_out, C, notD_out);
  and and_5 (and_5_out, notB_out, notD_out);
  and and_6 (and_6_out, C, notD_out);
  and and_7 (and_7_out, B, notD_out);
  and and_8 (and_8_out, B, notC_out);
  and and_9 (and_9_out, notC_out, notD_out);
  and and_10 (and_10_out, C, notD_out);
  or or_2 (or_2_out, A, C);
  xnor xnor_2 (xnor_2_out, B, D);
  or or_3 (C_seg, or_1_out, D);
  or or_4 (or_4_out, and_1_out, and_2_out);
  and and_11 (and_11_out, and_3_out, D);
  or or_5 (E_seg, and_5_out, and_6_out);
  or or_6 (or_6_out, A, and_7_out);
  or or_7 (or_7_out, and_8_out, and_9_out);
  or or_8 (or_8_out, and_10_out, A);
  xor xor_1 (xor_1_out, B, C);
  or or_9 (A_seg, or_2_out, xnor_2_out);
  or or_10 (B_seg, xnor_1_out, notB_out);
  or or_11 (or_11_out, or_4_out, and_11_out);
  or or_12 (F_seg, or_6_out, or_7_out);
  or or_13 (G_seg, or_8_out, xor_1_out);
  or or_14 (D_seg, or_11_out, and_4_out);
  _7_Segment_Display u_7_segment_display_1 (
    .g(G_seg), .f(F_seg), .a(A_seg), .b(B_seg), .e(E_seg), .d(D_seg), .c(C_seg));  // open: dp
  xnor xnor_3 (out_14, in_5, in_6);

  // Notes on the sheet:
  //   A
  //   B
  //   C
  //   D
  //   E
  //   F
  //   G
endmodule
